# Fritzing sketch game console (saved by Fritzing 0.9.3b)
circuit board: 5cm x 7.6cm

parts:
  J1 = female pin header, 1 pin [form="♀ (female)"]
  Btn = Momentary Switch [package=ksa_sealed_tac_switch]
  Nano = Arduino Nano (Rev3.0)
  LiPo_Charger = Micro Lipo Charger
  VIN = female pin header, 1 pin [form="♀ (female)"]
  OLED = OLED 128x64 I2C Monochrome Display GND-VDD

nets:
  N1: J1.pin1, LiPo_Charger.VBAT
  GND: Btn.2, Nano.GND, LiPo_Charger.GND, OLED.GND
  N2: Btn.4, Nano.D12/MISO
  N3: Nano.VIN, VIN.pin1
  N4: Nano.A5, OLED.SCK
  N5: Nano.A4, OLED.SDA
  3V3: Nano.3V3, OLED.VDD

notes:
  Mastoras Inc
  On/Off

custom parts:
  Micro Lipo Charger: Oh so handy, this little lipo charger is so small and easy to use you can keep it on your desk or mount it easily into any project! Simply plug it via any MicroUSB cable into a USB port and a 3.7V/4.2V lithium polymer or lithium ion rechargeable battery into the JST plug on the other end. There are two LEDs - one red and one green. While charging, the red LED is lit. When the battery is fully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
  OLED 128x64 I2C Monochrome Display GND-VDD: OLED 128x64 I2C Monochrome Display. Note: there are two variants of this part, this one is the GND VDD SCK SDA variant. The other is VDD GND SCK SDA. Make sure you select the part that matches your module as using the incorrect part will probably destroy your module! In addition the mounting holes are marked on silkscreen but not by default drilled. If you want drilled mounting holes, copy a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
